# Fritzing sketch RGB-Wiring (saved by Fritzing 0.9.3b)
breadboards: 1

parts:
  Part1 = Arduino Pro Mini v13
  Q1 = Basic FET N-Channel [package="D2Pak [SMD]"]
  Q2 = Basic FET N-Channel [package="D2Pak [SMD]"]
  Q3 = Basic FET N-Channel [package="D2Pak [SMD]"]
  R1 = Resistor [tolerance=±5% resistance=220 package=THT]
  R2 = Resistor [tolerance=±5% resistance=220 package=THT]
  R3 = Resistor [tolerance=±5% resistance=220 package=THT]
  LED1 = RGB LED (com. cathode, rgb) [package="5 mm [THT]"]  # not connected
  J1 = Power Jack [package=power_jack_combo]
  R4 = Resistor [tolerance=±5% resistance=220 package="0603 [SMD]"]
  R9 = Rotary Potentiometer (Small) [maximum_resistance=100kΩ package=THT]

nets:
  N1: Part1.GND, Q1.source, Q2.source, Q3.source, J1.GNDBREAK, R9.leg1
  N2: Part1.A3, R4.Pin_1
  N3: Part1.D11_PWM/MOSI, R3.Pin_0
  N4: Part1.D10_PWM/SS, R1.Pin_0
  N5: Part1.D9_PWM, R2.Pin_0
  N6: Q1.Gate, R3.Pin_1
  N7: Q2.Gate, R1.Pin_1
  N8: Q3.Gate, R2.Pin_1
  N9: J1.PWR, R9.leg2
  N10: R4.Pin_0, R9.wiper
